# Fritzing sketch sketch (saved by Fritzing 0.9.3b)
breadboards: 1

parts:
  WeMos_D1_Mini1 = WeMos D1 Mini
  R3 = Resistor [tolerance=±5% resistance=2.2k package="2512 [SMD]"]
  R4 = Resistor [tolerance=±5% resistance=2.2k package="2512 [SMD]"]
  R5 = Resistor [tolerance=±5% resistance=2.2k package="2512 [SMD]"]
  R6 = Resistor [tolerance=±5% resistance=10k package="0603 [SMD]"]
  R1 = Resistor [tolerance=±5% resistance=10k package="0603 [SMD]"]
  R7 = Resistor [tolerance=±5% resistance=10k package="0603 [SMD]"]
  R8 = Resistor [tolerance=±5% resistance=10k package="0603 [SMD]"]  # not connected
  R2 = Resistor [tolerance=±5% resistance=2.2k package="2512 [SMD]"]
  HLK-PM1 = HLK-PM12 [part_number=HLK-PM12]
  VCC1 = Battery  # not connected

nets:
  N1: WeMos_D1_Mini1.D1, R4.Pin_1
  N2: WeMos_D1_Mini1.D2, R2.Pin_0
  N3: WeMos_D1_Mini1.D6, R5.Pin_1
  N4: WeMos_D1_Mini1.D7, R3.Pin_0
  N5: WeMos_D1_Mini1.G, R6.Pin_0, R1.Pin_1, R7.Pin_1, HLK-PM1.-Vo

notes:
  12V common ground
  12V+ (D1 signal)
  12V+ (D0 signal)
  2K ohm resistors
  10K ohm resistors (pull-down)
  3.3 VCC
  12 VCC
  WG Reader (1)
  WG Reader (2)
